// Logisim project Bloco de memória.circ as structural Verilog: 1 circuit, main circuit main
module main (
  input  [7:0] in_1,
  input  Store,
  input  [7:0] in_3,
  input  Clock,
  output [7:0] out_5
);

  wire not_1_out;

  assign out_5 = Store ? in_1 : 8'bz;  // Controlled_Buffer controlled_buffer_1
  RAM ram_1 (.addr(in_3), .data(out_5), .clk(Clock), .ld(not_1_out));  // open: sel, clr
  not not_1 (not_1_out, Store);

  // Notes on the sheet:
  //   Store Data
  //   Address
  //   Load/Store Data
endmodule
