// Logisim project Decodificador - 3.circ as structural Verilog: 1 circuit, main circuit main
module main (
  input  in_1,
  input  in_2,
  input  in_3,
  output out_4,
  output out_5,
  output out_6,
  output out_7,
  output out_8,
  output out_9,
  output out_10,
  output out_11
);

  wire and_1_out, and_3_out, and_5_out, nor_2_out, nor_3_out, nor_4_out, not_1_out, not_2_out, not_3_out;

  not not_1 (not_1_out, in_3);
  not not_2 (not_2_out, in_2);
  not not_3 (not_3_out, in_1);
  nor nor_1 (out_4, in_1, in_2, in_3);
  nor nor_2 (nor_2_out, in_3, in_2);
  nor nor_3 (nor_3_out, in_1, in_3);
  and and_1 (and_1_out, in_1, in_2);
  and and_2 (out_7, and_1_out, not_1_out);
  nor nor_4 (nor_4_out, in_1, in_2);
  and and_3 (and_3_out, in_1, in_3);
  and and_4 (out_9, and_3_out, not_2_out);
  and and_5 (and_5_out, in_2, in_3);
  and and_6 (out_10, and_5_out, not_3_out);
  and and_7 (out_11, in_1, in_2, in_3);
  and and_8 (out_5, in_1, nor_2_out);
  and and_9 (out_6, nor_3_out, in_2);
  and and_10 (out_8, nor_4_out, in_3);
endmodule
