// Logisim project Decodificador - 4 - Display.circ as structural Verilog: 1 circuit, main circuit main
module main (
  input  in_1,
  input  in_2,
  input  in_3,
  input  in_4
);

  wire and_1_out, and_2_out, and_3_out, and_4_out, and_5_out, and_6_out, and_7_out, and_8_out, and_9_out,
       and_10_out, and_11_out, and_12_out, and_13_out, and_14_out, and_15_out, and_16_out, and_17_out,
       and_18_out, and_19_out, and_20_out, and_21_out, and_22_out, and_23_out, and_24_out, and_25_out,
       and_26_out, nor_1_out, nor_2_out, nor_3_out, nor_4_out, nor_5_out, nor_6_out, nor_7_out, nor_8_out,
       nor_9_out, not_1_out, not_2_out, not_3_out, not_4_out, not_5_out, not_6_out, or_1_out, or_2_out,
       or_3_out, or_4_out, or_5_out, or_6_out, or_7_out, or_8_out, or_9_out, or_10_out;

  and and_1 (and_1_out, in_4, and_5_out);
  nor nor_1 (nor_1_out, in_1, in_3, in_2);
  nor nor_2 (nor_2_out, in_3, in_2);
  nor nor_3 (nor_3_out, in_1, in_3);
  and and_2 (and_2_out, in_1, in_2);
  not not_1 (not_1_out, in_3);
  nor nor_4 (nor_4_out, in_1, in_2);
  and and_3 (and_3_out, in_1, in_3);
  not not_2 (not_2_out, in_2);
  and and_4 (and_4_out, in_2, in_3);
  not not_3 (not_3_out, in_1);
  and and_5 (and_5_out, in_1, in_2, in_3);
  not not_4 (not_4_out, in_4);
  and and_6 (and_6_out, in_4, and_12_out);
  and and_7 (and_7_out, in_4, and_13_out);
  not not_5 (not_5_out, in_4);
  and and_8 (and_8_out, nor_2_out, in_1);
  and and_9 (and_9_out, nor_3_out, in_2);
  and and_10 (and_10_out, and_2_out, not_1_out);
  and and_11 (and_11_out, nor_4_out, in_3);
  and and_12 (and_12_out, and_3_out, not_2_out);
  and and_13 (and_13_out, and_4_out, not_3_out);
  and and_14 (and_14_out, in_4, and_11_out);
  and and_15 (and_15_out, not_5_out, nor_1_out);
  and and_16 (and_16_out, not_4_out, and_8_out);
  and and_17 (and_17_out, not_4_out, and_9_out);
  and and_18 (and_18_out, not_4_out, and_10_out);
  and and_19 (and_19_out, not_4_out, and_11_out);
  and and_20 (and_20_out, not_4_out, and_12_out);
  and and_21 (and_21_out, not_4_out, and_13_out);
  and and_22 (and_22_out, and_5_out, not_4_out);
  and and_23 (and_23_out, nor_1_out, in_4);
  and and_24 (and_24_out, and_8_out, in_4);
  and and_25 (and_25_out, and_9_out, in_4);
  and and_26 (and_26_out, and_10_out, in_4);
  LED led_1 (.in(and_15_out));
  LED led_2 (.in(and_16_out));
  LED led_3 (.in(and_17_out));
  LED led_4 (.in(and_18_out));
  LED led_5 (.in(and_19_out));
  LED led_6 (.in(and_20_out));
  LED led_7 (.in(and_21_out));
  LED led_8 (.in(and_22_out));
  LED led_9 (.in(and_23_out));
  LED led_10 (.in(and_24_out));
  LED led_11 (.in(and_25_out));
  LED led_12 (.in(and_26_out));
  LED led_13 (.in(and_14_out));
  LED led_14 (.in(and_6_out));
  LED led_15 (.in(and_7_out));
  LED led_16 (.in(and_1_out));
  or or_1 (or_1_out, and_25_out, and_15_out);
  or or_2 (or_2_out, and_26_out, and_16_out);
  or or_3 (or_3_out, and_17_out, and_14_out);
  or or_4 (or_4_out, and_18_out, and_6_out);
  or or_5 (or_5_out, and_19_out, and_7_out);
  or or_6 (or_6_out, and_20_out, and_1_out);
  or or_7 (or_7_out, and_15_out, and_16_out, and_17_out, and_18_out, and_19_out, and_20_out, and_21_out, and_22_out, and_23_out, and_24_out);
  or or_8 (or_8_out, and_25_out, and_26_out, and_14_out, and_6_out, and_7_out, and_1_out);
  or or_9 (or_9_out, or_7_out, or_8_out);
  _7_Segment_Display u_7_segment_display_1 (
    .f(or_7_out), .a(or_7_out), .b(or_9_out), .e(or_7_out), .d(or_7_out), .c(or_9_out));  // open: g, dp
  _7_Segment_Display u_7_segment_display_2 (
    .g(nor_9_out), .f(nor_5_out), .a(nor_6_out), .b(nor_7_out), .e(or_10_out), .d(nor_8_out), .c(not_6_out));  // open: dp
  nor nor_5 (nor_5_out, or_2_out, or_3_out, or_4_out, and_22_out);
  nor nor_6 (nor_6_out, or_2_out, or_5_out);
  nor nor_7 (nor_7_out, or_6_out, and_21_out);
  or or_10 (or_10_out, or_1_out, or_3_out, and_21_out, and_23_out);
  nor nor_8 (nor_8_out, or_2_out, or_5_out, and_22_out);
  not not_6 (not_6_out, or_3_out);
  nor nor_9 (nor_9_out, or_1_out, or_2_out, and_22_out);
endmodule
