// Logisim project Decodificador - 4.circ as structural Verilog: 1 circuit, main circuit main
module main (
  input  in_1,
  input  in_2,
  input  in_3,
  input  in_4,
  output out_5,
  output out_6,
  output out_7,
  output out_8,
  output out_9,
  output out_10,
  output out_11,
  output out_12,
  output out_13,
  output out_14,
  output out_15,
  output out_16,
  output out_17,
  output out_18,
  output out_19,
  output out_20
);

  wire and_2_out, and_3_out, and_4_out, and_5_out, and_8_out, and_9_out, and_10_out, and_11_out, and_12_out,
       and_13_out, nor_1_out, nor_2_out, nor_3_out, nor_4_out, not_1_out, not_2_out, not_3_out, not_4_out,
       not_5_out;

  and and_1 (out_20, in_4, and_5_out);
  nor nor_1 (nor_1_out, in_1, in_3, in_2);
  nor nor_2 (nor_2_out, in_3, in_2);
  nor nor_3 (nor_3_out, in_1, in_3);
  and and_2 (and_2_out, in_1, in_2);
  not not_1 (not_1_out, in_3);
  nor nor_4 (nor_4_out, in_1, in_2);
  and and_3 (and_3_out, in_1, in_3);
  not not_2 (not_2_out, in_2);
  and and_4 (and_4_out, in_2, in_3);
  not not_3 (not_3_out, in_1);
  and and_5 (and_5_out, in_1, in_2, in_3);
  not not_4 (not_4_out, in_4);
  and and_6 (out_18, in_4, and_12_out);
  and and_7 (out_19, in_4, and_13_out);
  not not_5 (not_5_out, in_4);
  and and_8 (and_8_out, nor_2_out, in_1);
  and and_9 (and_9_out, nor_3_out, in_2);
  and and_10 (and_10_out, and_2_out, not_1_out);
  and and_11 (and_11_out, nor_4_out, in_3);
  and and_12 (and_12_out, and_3_out, not_2_out);
  and and_13 (and_13_out, and_4_out, not_3_out);
  and and_14 (out_17, in_4, and_11_out);
  and and_15 (out_5, not_5_out, nor_1_out);
  and and_16 (out_6, not_4_out, and_8_out);
  and and_17 (out_7, not_4_out, and_9_out);
  and and_18 (out_8, not_4_out, and_10_out);
  and and_19 (out_9, not_4_out, and_11_out);
  and and_20 (out_10, not_4_out, and_12_out);
  and and_21 (out_11, not_4_out, and_13_out);
  and and_22 (out_12, and_5_out, not_4_out);
  and and_23 (out_13, nor_1_out, in_4);
  and and_24 (out_14, and_8_out, in_4);
  and and_25 (out_15, and_9_out, in_4);
  and and_26 (out_16, and_10_out, in_4);
endmodule
