// Logisim project Flip Flop - D - Copia.circ as structural Verilog: 1 circuit, main circuit main
module main (
  input  in_1,
  input  in_2,
  input  in_3,
  input  in_4,
  input  in_5
);

  wire and_1_out, and_2_out, clock_1_out, clock_2_out, nand_1_out, nor_1_out, nor_2_out, nor_3_out,
       not_1_out, not_2_out;
  wire [3:0] bitselector_1_out, bitselector_2_out, bitselector_3_out, bitselector_4_out, counter_1_q,
       counter_2_q, counter_3_q, counter_4_q, counter_5_q;

  Clock clock_1 (.out(clock_1_out));
  Hex_Digit_Display hex_digit_display_1 ();  // open: value, dp
  Hex_Digit_Display hex_digit_display_2 ();  // open: value, dp
  // Probe on counter_1_q
  Counter #(.width(4), .max('h9)) counter_1 (
    .load(in_4), .count(in_5), .Q(counter_1_q), .clk(clock_1_out));  // open: D, carry, clr
  not not_1 (not_1_out, counter_1_q[3]);
  not not_2 (not_2_out, counter_1_q[0]);
  nand nand_1 (nand_1_out, counter_1_q[2], counter_1_q[1]);
  Hex_Digit_Display hex_digit_display_3 ();  // open: value, dp
  Hex_Digit_Display hex_digit_display_4 ();  // open: value, dp
  and and_1 (and_1_out, not_1_out, not_2_out);
  and and_2 (and_2_out, nand_1_out, and_1_out);
  Hex_Digit_Display hex_digit_display_5 (.value(bitselector_4_out));  // open: dp
  LED led_1 (.in(clock_2_out));
  Clock clock_2 (.out(clock_2_out));
  nor nor_1 (nor_1_out, bitselector_1_out[0], bitselector_1_out[1], bitselector_1_out[2], bitselector_1_out[3]);
  nor nor_2 (nor_2_out, bitselector_2_out[0], bitselector_2_out[1], bitselector_2_out[2], bitselector_2_out[3]);
  nor nor_3 (nor_3_out, bitselector_3_out[0], bitselector_3_out[1], bitselector_3_out[2], bitselector_3_out[3]);
  Hex_Digit_Display hex_digit_display_6 (.value(bitselector_3_out));  // open: dp
  Hex_Digit_Display hex_digit_display_7 (.value(bitselector_2_out));  // open: dp
  BitSelector #(.width(4), .group(4)) bitselector_1 (.in(counter_2_q), .out(bitselector_1_out), .sel(in_3));
  Counter #(.width(4), .max('h9)) counter_2 (
    .load(in_1), .count(in_2), .Q(counter_2_q), .clk(clock_2_out));  // open: D, carry, clr
  Counter #(.width(4), .max('h5)) counter_3 (
    .count(in_2), .Q(counter_3_q), .clk(nor_1_out));  // open: load, D, carry, clr
  BitSelector #(.width(4), .group(4)) bitselector_2 (.in(counter_3_q), .out(bitselector_2_out), .sel(in_3));
  Counter #(.width(4), .max('h9)) counter_4 (
    .count(in_2), .Q(counter_4_q), .clk(nor_2_out));  // open: load, D, carry, clr
  BitSelector #(.width(4), .group(4)) bitselector_3 (.in(counter_4_q), .out(bitselector_3_out), .sel(in_3));
  BitSelector #(.width(4), .group(4)) bitselector_4 (.in(counter_5_q), .out(bitselector_4_out), .sel(in_3));
  Counter #(.width(4), .max('h5)) counter_5 (
    .count(in_2), .Q(counter_5_q), .clk(nor_3_out));  // open: load, D, carry, clr
  Hex_Digit_Display hex_digit_display_8 (.value(bitselector_1_out));  // open: dp
endmodule
