// Logisim project Flip Flop - D.circ as structural Verilog: 1 circuit, main circuit main
module main (
  input  D,
  input  Clo,
  input  Clo_2,
  input  D_2,
  input  Presset,
  input  Enable,
  input  Clear,
  output Q,
  output Q_2,
  output Q_prime,
  output Q_prime_2
);

  wire nand_1_out, nand_2_out, nand_3_out;

  nand nand_1 (nand_1_out, D, Clo_2);
  nand nand_2 (nand_2_out, Clo_2, nand_3_out);
  nand nand_3 (nand_3_out, D, D);
  nand nand_4 (Q, nand_1_out, Q_prime);
  nand nand_5 (Q_prime, Q, nand_2_out);
  D_Flip_Flop d_ff_1 (.clk(Clo), .D(D_2), .Q(Q_2), .Qn(Q_prime_2), .preset(Presset), .en(Enable), .reset(Clear));

  // Notes on the sheet:
  //   Flip Flop - D
endmodule
