// Logisim project Joystik.circ as structural Verilog: 1 circuit, main circuit main
module main (
  output [1:0] out_1,
  output [1:0] out_2
);

  wire and_1_out, and_2_out, and_3_out, and_4_out, and_5_out, and_6_out, and_7_out, and_8_out, and_9_out,
       and_10_out, and_11_out, and_12_out, and_13_out, and_14_out, and_15_out, and_16_out, and_17_out,
       nor_1_out, nor_2_out, nor_3_out, nor_4_out, nor_5_out, nor_6_out, nor_7_out, nor_8_out, nor_9_out,
       not_1_out, not_2_out, not_3_out, not_4_out, not_5_out, or_1_out;

  _7_Segment_Display u_7_segment_display_1 (
    .g(nor_9_out), .f(nor_8_out), .a(nor_7_out), .b(nor_6_out), .e(or_1_out), .d(nor_5_out), .c(not_5_out));  // open: dp
  Joystick #(.bits(2)) joystick_1 (.x(out_1), .y(out_2));
  nor nor_1 (nor_1_out, out_1[0], out_2[0]);
  and and_1 (and_1_out, out_1[1], out_2[1]);
  nor nor_2 (nor_2_out, out_1[0], out_2[1]);
  and and_2 (and_2_out, out_1[1], out_2[0]);
  and and_3 (and_3_out, out_1[1], out_2[0], out_2[1]);
  not not_1 (not_1_out, out_1[0]);
  and and_4 (and_4_out, out_1[0], out_1[1], out_2[1]);
  not not_2 (not_2_out, out_2[0]);
  nor nor_3 (nor_3_out, out_1[1], out_2[0]);
  and and_5 (and_5_out, out_1[0], out_2[1]);
  and and_6 (and_6_out, out_1[0], out_1[1], out_2[0]);
  not not_3 (not_3_out, out_2[1]);
  and and_7 (and_7_out, out_1[0], out_1[1], out_2[0], out_2[1]);
  and and_8 (and_8_out, out_1[0], out_2[0], out_2[1]);
  not not_4 (not_4_out, out_1[1]);
  nor nor_4 (nor_4_out, out_1[1], out_2[1]);
  and and_9 (and_9_out, out_1[0], out_2[0]);
  and and_10 (and_10_out, nor_1_out, and_1_out);
  and and_11 (and_11_out, nor_2_out, and_2_out);
  and and_12 (and_12_out, and_3_out, not_1_out);
  and and_13 (and_13_out, and_4_out, not_2_out);
  and and_14 (and_14_out, nor_3_out, and_5_out);
  and and_15 (and_15_out, and_6_out, not_3_out);
  and and_16 (and_16_out, and_8_out, not_4_out);
  and and_17 (and_17_out, nor_4_out, and_9_out);
  or or_1 (or_1_out, and_10_out, and_12_out, and_7_out, and_17_out);
  not not_5 (not_5_out, and_12_out);
  nor nor_5 (nor_5_out, and_11_out, and_14_out, and_16_out);
  nor nor_6 (nor_6_out, and_15_out, and_7_out);
  nor nor_7 (nor_7_out, and_11_out, and_14_out);
  nor nor_8 (nor_8_out, and_11_out, and_12_out, and_13_out, and_16_out);
  nor nor_9 (nor_9_out, and_10_out, and_11_out, and_16_out);
endmodule
