// Logisim project Portas lógicas.circ as structural Verilog: 1 circuit, main circuit main
module main (
  input  OR,
  input  A,
  input  in_3,
  input  B,
  input  A_2,
  input  A_3,
  input  A_4,
  input  B_2,
  input  B_3,
  input  A_5,
  input  A_6,
  input  B_4,
  input  B_5,
  output out_14,
  output out_15,
  output NOT,
  output out_17,
  output out_18,
  output out_19,
  output out_20
);

  wire and_2_out, and_3_out, and_4_out, and_5_out, and_6_out, not_1_out, not_2_out, not_4_out, not_5_out,
       or_3_out, or_4_out;

  or or_1 (out_14, OR, in_3);
  and and_1 (out_17, A_3, B_2);
  not not_1 (not_1_out, A_5);
  not not_2 (not_2_out, B_4);
  and and_2 (and_2_out, not_1_out, B_4);
  and and_3 (and_3_out, A_5, not_2_out);
  not not_3 (NOT, A_2);
  or or_2 (out_19, and_2_out, and_3_out);
  not not_4 (not_4_out, A_6);
  and and_4 (and_4_out, not_4_out, B_5);
  and and_5 (and_5_out, A_6, not_5_out);
  not not_5 (not_5_out, B_5);
  not not_6 (out_15, or_3_out);
  or or_3 (or_3_out, A, B);
  not not_7 (out_18, and_6_out);
  and and_6 (and_6_out, A_4, B_3);
  or or_4 (or_4_out, and_4_out, and_5_out);
  not not_8 (out_20, or_4_out);

  // Notes on the sheet:
  //   AND
  //   XOR
  //   NOR
  //   NAND
  //   XNOR
endmodule
