// Logisim project Registradores.circ as structural Verilog: 1 circuit, main circuit main
module main (
  input  Clo,
  input  Reset,
  input  \D¹ ,
  input  \D² ,
  input  \D³ ,
  input  \D⁴ ,
  output \Q¹ ,
  output \Q² ,
  output \Q³ ,
  output \Q⁴ 
);

  D_Flip_Flop d_ff_1 (.clk(Clo), .D(\D¹ ), .Q(\Q¹ ), .reset(Reset));  // open: Qn, preset, en
  D_Flip_Flop d_ff_2 (.clk(Clo), .D(\D² ), .Q(\Q² ), .reset(Reset));  // open: Qn, preset, en
  D_Flip_Flop d_ff_3 (.clk(Clo), .D(\D³ ), .Q(\Q³ ), .reset(Reset));  // open: Qn, preset, en
  D_Flip_Flop d_ff_4 (.clk(Clo), .D(\D⁴ ), .Q(\Q⁴ ), .reset(Reset));  // open: Qn, preset, en
endmodule
